// Logisim project Exercicio_70x.circ as structural Verilog: 4 circuits, main circuit Exercicio_701
module Exercicio_701 (
  input  A,
  input  B,
  input  S,
  output out_4,
  output out_5
);

  wire and_1_out, and_2_out, nand_1_out, nand_2_out, nand_3_out;

  nand nand_1 (nand_1_out, S, S);
  and and_1 (and_1_out, B, S);
  and and_2 (and_2_out, A, nand_1_out);
  nand nand_2 (nand_2_out, and_2_out, and_2_out);
  nand nand_3 (nand_3_out, and_1_out, and_1_out);
  nand nand_4 (out_4, nand_2_out, nand_3_out);
  and and_3 (out_5, nand_2_out, nand_3_out);
endmodule

module Exercicio_702 (
  input  A,
  input  B,
  input  S,
  output out_4
);

  wire nor_1_out, nor_2_out, nor_3_out, nor_4_out, nor_5_out, nor_6_out, nor_7_out;

  not nor_1 (nor_1_out, S);  // NOR_Gate
  not nor_2 (nor_2_out, B);  // NOR_Gate
  not nor_3 (nor_3_out, S);  // NOR_Gate
  not nor_4 (nor_4_out, A);  // NOR_Gate
  not nor_5 (nor_5_out, nor_1_out);  // NOR_Gate
  nor nor_6 (nor_6_out, nor_2_out, nor_3_out);
  nor nor_7 (nor_7_out, nor_4_out, nor_5_out);
  or or_1 (out_4, nor_7_out, nor_6_out);
endmodule

module Exercicio_703 (
  input  A,
  input  B,
  input  S,
  output out_4,
  output out_5,
  output out_6
);

  wire and_1_out, and_2_out, nand_1_out, nand_2_out, nand_3_out, nor_1_out, nor_2_out, nor_3_out, nor_4_out,
       nor_5_out, nor_6_out, nor_7_out;

  not nor_1 (nor_1_out, S);  // NOR_Gate
  not nor_2 (nor_2_out, B);  // NOR_Gate
  nand nand_1 (nand_1_out, S, S);
  not nor_3 (nor_3_out, A);  // NOR_Gate
  not nor_4 (nor_4_out, nor_1_out);  // NOR_Gate
  nor nor_5 (nor_5_out, nor_2_out, nor_6_out);
  not nor_6 (nor_6_out, S);  // NOR_Gate
  and and_1 (and_1_out, A, nand_1_out);
  and and_2 (and_2_out, B, S);
  nor nor_7 (nor_7_out, nor_3_out, nor_4_out);
  or or_1 (out_6, nor_7_out, nor_5_out);
  nand nand_2 (nand_2_out, and_1_out, and_1_out);
  nand nand_3 (nand_3_out, and_2_out, and_2_out);
  nand nand_4 (out_4, nand_2_out, nand_3_out);
  Multiplexer multiplexer_1 (.in0(out_4), .in1(out_4), .out(out_5), .sel(S));  // open: en
endmodule

module Exercicio_704 (
  input  in_1,
  input  in_2,
  input  in_3,
  output out_4,
  output out_5
);

  wire xnor_2_out, xnor_3_out;

  xnor xnor_1 (out_4, in_1, in_2);
  not xnor_2 (xnor_2_out, in_1);  // XNOR_Gate
  not xnor_3 (xnor_3_out, in_2);  // XNOR_Gate
  nor nor_1 (out_5, xnor_2_out, xnor_3_out);
endmodule
